# Fritzing sketch SmarThermo (saved by Fritzing 0.9.4)
breadboards: 1

parts:
  Raspberry_Pi_Zero1 = Raspberry Pi Zero  # not connected
  DS3 = DS18B20 1-Wire Temperature Sensor Probe Cable
  R1 = Resistor [tolerance=±5% resistance=4.7 package="0805 [SMD]"]
  MCU1 = Raspberry Pi Zero

nets:
  N1: DS3.GND, MCU1.pin_6, MCU1.pin_9, MCU1.pin_20
  N2: DS3.DQ, R1.Pin_0, MCU1.pin_7
  N3: DS3.VDD, R1.Pin_1, MCU1.pin_1, MCU1.pin_17

notes:
  DS18B20
